// Logisim project alu.circ as structural Verilog: 1 circuit, main circuit alu
module alu (
  input  [31:0] A,
  input  [31:0] B,
  input  [3:0] ALUSel,
  output [31:0] Result
);

  wire comparator_1_lt;
  wire [4:0] bit_extender_1_out, bit_extender_2_out, bit_extender_3_out;
  wire [31:0] add, and_, div_, mul_, mulh_, or_, rem_, sll_, slt_, sra_, srl_, sub_, xor_;

  Adder #(.width(32)) adder_1 (.a(A), .b(B), .out(add));  // open: cin, cout
  assign and_ = A & B;  // AND_Gate and_1, 32 bits wide
  assign or_ = A | B;  // OR_Gate or_1, 32 bits wide
  assign xor_ = A ^ B;  // XOR_Gate xor_1, 32 bits wide
  Bit_Extender #(.in_width(32), .out_width(5)) bit_extender_1 (.in(B), .out(bit_extender_1_out));
  Bit_Extender #(.in_width(32), .out_width(5)) bit_extender_2 (.in(B), .out(bit_extender_2_out));
  Bit_Extender #(.in_width(32), .out_width(5)) bit_extender_3 (.in(B), .out(bit_extender_3_out));
  Comparator #(.width(32)) comparator_1 (.a(A), .b(B), .lt(comparator_1_lt));  // open: gt, eq
  Divider #(.width(32)) divider_1 (.a(A), .b(B), .out(div_));  // open: upper, rem
  Divider #(.width(32)) divider_2 (.a(A), .b(B), .rem(rem_));  // open: out, upper
  Multiplier #(.width(32)) multiplier_1 (.a(A), .b(B), .out(mul_));  // open: cin, cout
  Multiplier #(.width(32)) multiplier_2 (.a(A), .b(B), .cout(mulh_));  // open: out, cin
  Subtractor #(.width(32)) subtractor_1 (.a(A), .b(B), .out(sub_));  // open: bin, bout
  Shifter #(.width(32), .shift("lr")) shifter_1 (.in(A), .\dist (bit_extender_1_out), .out(srl_));
  Shifter #(.width(32), .shift("ar")) shifter_2 (.in(A), .\dist (bit_extender_2_out), .out(sra_));
  Shifter #(.width(32)) shifter_3 (.in(A), .\dist (bit_extender_3_out), .out(sll_));
  assign slt_ = {{31{1'b0}}, comparator_1_lt};  // Bit_Extender bit_extender_4
  Multiplexer #(.select(4), .width(32), .enable("false")) multiplexer_1 (
    .in0(add), .in1(and_), .in2(or_), .in3(xor_), .in4(srl_), .in5(sra_), .in6(sll_), .in7(slt_), .in8(div_),
    .in9(rem_), .in10(mul_), .in11(mulh_), .in12(sub_), .in13(B), .out(Result), .sel(ALUSel));  // open: in14, in15

  // Other names for the same wires on the sheet: bsel[31:0] = B

  // Notes on the sheet:
  //   INPUTS to your circuit
  //   DON'T CHANGE THE LOCATIONS OF THE INPUTS AND OUTPUTS!
  //   OUTPUT from your circuit
endmodule
